# Fritzing sketch ballotbox1 (saved by Fritzing 0.9.2b)
breadboards: 1

parts:
  Controller = Arduino Uno (Rev3)
  Linear_Regulator = Voltage Regulator [part_number=LM317 package=to220-adj]
  DC_Adapter = DC Power [voltage=12V]
  part = Trimmer Potentiometer [maximum_resistance=5kΩ package=THT]
  Diverter_Servo = Basic Servo [part_number=6001HB]
  Motor_Driver = L293D [package=THT]
  Feed_Motor = DC Motor
  D1 = Diode [package=diode-1n4001]
  D2 = Diode [package=diode-1n4001]
  D3 = Diode [package=diode-1n4001]
  D4 = Diode [package=diode-1n4001]
  Reject_Mode = Pushbutton [package=THT]
  Feed_Sensor = PHOTOTRANSISTOR REFLECTIVE OBJECT SENSOR [part_number=HY301-21 package=qrb1114-side]
  part_2 = Resistor [tolerance=±5% resistance=220 package=THT]
  LED1 = LED - 5mm [color="Red (633nm)" package="5 mm [THT]"]
  part_3 = Resistor [tolerance=±5% resistance=1k package=THT]
  Feed_Sensor_2 = PHOTOTRANSISTOR REFLECTIVE OBJECT SENSOR [part_number=HY301-21 package=qrb1114-side]
  part_4 = Resistor [tolerance=±5% resistance=220 package=THT]
  LED2 = LED - 5mm [color="Red (633nm)" package="5 mm [THT]"]
  part_5 = Resistor [tolerance=±5% resistance=1k package=THT]
  Sound_Controller = Arduino Uno (Rev3)
  PC_speaker = SPEAKER [package=pcb_mount_speaker]
  Experimenter_Button = Pushbutton [package=THT]

nets:
  N1: Controller.A2, Feed_Sensor.E, part_3.Pin_0
  N2: Controller.A3, Feed_Sensor_2.E, part_5.Pin_0
  N3: Controller.D8, Motor_Driver.In_1
  N4: Controller.D9_PWM, Diverter_Servo.pulse
  N5: Controller.D10_PWM/SS, Sound_Controller.D10_PWM/SS
  N6: Controller.D11_PWM/MOSI, Sound_Controller.D11_PWM/MOSI
  N7: Controller.D12/MISO, Sound_Controller.D12/MISO
  GND: Controller.GND, DC_Adapter.V-, part.leg1, Diverter_Servo.gnd, Motor_Driver.0V, D3.A, D4.A, Reject_Mode.leg1, Feed_Sensor.K, part_3.Pin_1, Feed_Sensor_2.K, part_5.Pin_1, Sound_Controller.GND, PC_speaker.-, Experimenter_Button.leg1
  N8: Controller.D3_PWM, Experimenter_Button.leg0
  N9: Controller.D5_PWM, Reject_Mode.leg0
  N10: Controller.D6_PWM, Motor_Driver.In_2
  N11: Controller.D7, Motor_Driver.Enable_1
  N12: Controller.5V, Motor_Driver.+V, part_2.Pin_0, LED1.anode, part_4.Pin_0, LED2.anode
  VIN: Controller.VIN, Linear_Regulator.IN, DC_Adapter.V+, Sound_Controller.VIN
  N13: Linear_Regulator.ADJ, part.leg2
  N14: Linear_Regulator.OUT, part.wiper, Diverter_Servo.vcc, Motor_Driver.+Vmotor, D1.C, D2.C
  N15: Motor_Driver.Out_1_(_Controlled_by_Enable_1_), Feed_Motor.pin_1, D1.A, D4.C
  N16: Motor_Driver.Out_2_(_Controlled_by_Enable_1_), Feed_Motor.pin_2, D2.A, D3.C
  N17: Feed_Sensor.A, part_2.Pin_1
  N18: Feed_Sensor.C, LED1.cathode
  N19: Feed_Sensor_2.A, part_4.Pin_1
  N20: Feed_Sensor_2.C, LED2.cathode
  N21: Sound_Controller.D8, PC_speaker.+

notes:
  5V
  0V
  12V
